# Fritzing sketch dak_schematic (saved by Fritzing 0.9.2b)
breadboards: 1

parts:
  Part1 = Arduino Nano (Rev3.0)
  D1 = LTE-302 [package=lte-302]
  D2 = LTE-302 [package=lte-302]
  R1 = Photocell (LDR) [package=THT]
  R2 = Photocell (LDR) [package=THT]
  Q1 = PNP-Transistor [package="SOT-23 [SMD]"]
  R3 = Resistor [tolerance=±5% resistance=6.8k package="2010 [SMD]"]
  R4 = Resistor [tolerance=±5% resistance=10k package="2010 [SMD]"]
  R5 = Resistor [tolerance=±5% resistance=10k package="2010 [SMD]"]
  C1 = Electrolytic Capacitor [capacitance=4.7µF package="0405 [SMD, electrolytic]"]
  PIR1 = PIR sensor
  U1 = FS1000A - 433Mhz RF Transmitter [package=THT]
  DHT1 = DHT11 Humitidy and Temperature Sensor

nets:
  GND: Part1.GND, Q1.2, R4.Pin_0, R5.Pin_0, C1.-, PIR1.GND, U1.GND
  N1: Part1.D2, DHT1.DATA
  N2: Part1.D4, PIR1.SIG
  N3: Part1.D9, U1.DATA
  VDD: Part1.5V, D1.A, D2.A, R1.pin_1, R2.pin_1, C1.+, PIR1.VDD, U1.VCC, DHT1.VDD
  N4: Part1.A1, R1.pin_0, R4.Pin_1
  N5: Part1.A0, R2.pin_0, R5.Pin_1
  N6: Part1.D13/SCK, R3.Pin_0
  N7: D1.C, D2.C, Q1.1
  N8: Q1.0, R3.Pin_1

notes:
  our part has 3 pins

custom parts:
  FS1000A - 433Mhz RF Transmitter: This is 433Mhz RF transmitter with receiver kit for Arduino ARM MCU wireless Application environment: Remote control switch, receiver module, motorcycles, automobile anti-theft products, home security products, electric doors, shutter doors, windows, remote control socket, remote control LED, remote audio remote control electric doors, garage door remote control, remote control retractable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
  DHT11 Humitidy and Temperature Sensor: DHT11 Humidity and Temperature Sensor
